# Fritzing sketch iRigate (saved by Fritzing 0.7.12b)
breadboards: 1

parts:
  U2 = atmega328 [package=dip]
  R1 = 10k Ω Resistor [package=THT]
  C5 = Ceramic Disk Capacitor [package=THT]
  LED4 = LED - 5mm [color="Green (565nm)" package="5 mm [THT]"]
  XTAL1 = Crystal [package=THT]
  C6 = Ceramic Disk Capacitor [package=THT]
  R2 = Resistor [tolerance=±5% resistance=220 package="0805 [SMD]"]
  WIFI-1 = Adafruit CC3000 WiFi Breakout
  TEMP-HUM-1 = AM2302 Humidity and Temperature Sensor
  MOSSFET-N = Basic FET N-Channel [package="TO220 [THT]"]
  VALVE1 = Plastic Solenoid Valve
  D2 = Rectifier Diode [part_number=1N4001 package="300 mil [THT]"]
  R3 = Resistor [tolerance=±5% resistance=10k package=THT]
  VCC1 = Battery block 9V
  U3 = Voltage Regulator - 5V [package="TO220 [THT]"]

nets:
  N1: U2.RESET, R1.Pin_1
  N2: U2.D2, TEMP-HUM-1.DATA
  N3: U2.D3_(PWM), WIFI-1.IRQ
  VCC: U2.VCC, U2.AVCC, U2.AREF, R1.Pin_0, WIFI-1.VIN, TEMP-HUM-1.VDD, VALVE1.no_name_yet#1, D2.cathode, VCC1.+, U3.input_voltage, U3.output_voltage
  N4: U2.GND#7, C5.pin_0, C6.pin_0, MOSSFET-N.source, R3.Pin_0
  N5: U2.XLAT1, XTAL1.pin_0, C6.pin_1
  N6: U2.XLAT2, C5.pin_1, XTAL1.pin_1
  N7: U2.D5_(PWM), WIFI-1.VBEN
  N8: U2.D6_(PWM), MOSSFET-N.gate, R3.Pin_1
  N9: U2.D10_(PWM), WIFI-1.CS
  N10: U2.D11_(PWM), WIFI-1.MOSI
  N11: U2.D12, WIFI-1.MISO
  N12: U2.D13, R2.Pin_0, WIFI-1.CLK
  GND: U2.GND#21, LED4.cathode, WIFI-1.GND, TEMP-HUM-1.GND, VCC1.-, U3.GND
  N13: LED4.anode, R2.Pin_1
  N14: MOSSFET-N.drain, VALVE1.no_name_yet#2, D2.anode

custom parts:
  Adafruit CC3000 WiFi Breakout: CC3000 WiFi Breakout
